// Logisim project SPM.circ as structural Verilog: 6 circuits, main circuit TCMP
module TCMP (
  input  A,
  input  clk,
  input  reset,
  output out_4
);

  wire d_ff_2_q, FDHA_out, or_1_out, xor_1_out;

  and FDHA (FDHA_out, A, d_ff_2_q);
  xor xor_1 (xor_1_out, A, d_ff_2_q);
  D_Flip_Flop #(.trigger("high")) d_ff_1 (.clk(clk), .D(xor_1_out), .Q(out_4), .reset(reset));  // open: Qn, preset, en
  or or_1 (or_1_out, A, d_ff_2_q);
  D_Flip_Flop #(.trigger("high")) d_ff_2 (
    .clk(clk), .D(or_1_out), .Q(d_ff_2_q), .reset(reset));  // open: Qn, preset, en
endmodule

module unit_digit (
  input  p3,
  input  p2,
  input  p1,
  input  p0,
  output a,
  output b,
  output c,
  output d,
  output e,
  output f,
  output g
);

  wire and_1_out, and_2_out, and_3_out, and_4_out, and_5_out, and_6_out, and_7_out, and_8_out, and_9_out,
       and_10_out, and_11_out, and_12_out, and_13_out, and_14_out, and_15_out, and_16_out, not_1_out,
       not_2_out, not_3_out, not_4_out, not_5_out, not_6_out, not_7_out, not_8_out, not_9_out, not_10_out,
       not_11_out, not_12_out, not_13_out, not_14_out, not_15_out, not_16_out, not_17_out, not_18_out,
       not_19_out, not_20_out, not_21_out;

  not not_1 (not_1_out, p2);
  and and_1 (and_1_out, not_1_out, not_2_out);
  not not_2 (not_2_out, p0);
  and and_2 (and_2_out, p2, p0);
  not not_3 (not_3_out, p2);
  not not_4 (not_4_out, p1);
  and and_3 (and_3_out, not_4_out, not_5_out);
  not not_5 (not_5_out, p0);
  and and_4 (and_4_out, p1, p0);
  not not_6 (not_6_out, p1);
  or or_1 (c, not_6_out, p0, p2);
  not not_7 (not_7_out, p2);
  and and_5 (and_5_out, not_7_out, not_8_out);
  not not_8 (not_8_out, p0);
  not not_9 (not_9_out, p2);
  and and_6 (and_6_out, not_9_out, p1);
  and and_7 (and_7_out, p1, not_10_out);
  not not_10 (not_10_out, p0);
  not not_11 (not_11_out, p1);
  and and_8 (and_8_out, p2, not_11_out, p0);
  not not_12 (not_12_out, p2);
  and and_9 (and_9_out, not_12_out, not_13_out);
  not not_13 (not_13_out, p0);
  and and_10 (and_10_out, p1, not_14_out);
  not not_14 (not_14_out, p0);
  not not_15 (not_15_out, p1);
  and and_11 (and_11_out, not_15_out, not_16_out);
  not not_16 (not_16_out, p0);
  and and_12 (and_12_out, p2, not_17_out);
  not not_17 (not_17_out, p1);
  and and_13 (and_13_out, p2, not_18_out);
  not not_18 (not_18_out, p0);
  not not_19 (not_19_out, p2);
  and and_14 (and_14_out, not_19_out, p1);
  and and_15 (and_15_out, p2, not_20_out);
  not not_20 (not_20_out, p1);
  and and_16 (and_16_out, p2, not_21_out);
  not not_21 (not_21_out, p0);
  or or_2 (a, and_1_out, p1, and_2_out, p3);
  or or_3 (b, not_3_out, and_3_out, and_4_out);
  or or_4 (d, and_5_out, and_6_out, and_7_out, and_8_out, p3);
  or or_5 (e, and_9_out, and_10_out);
  or or_6 (f, and_11_out, and_12_out, and_13_out, p3);
  or or_7 (g, and_14_out, and_15_out, and_16_out, p3);
endmodule

module HA (
  input  in_1,
  input  in_2,
  output out_3,
  output out_4
);

  xor xor_1 (out_3, in_1, in_2);
  and and_1 (out_4, in_1, in_2);
endmodule

module CSA (
  input  x,
  input  y,
  input  clr,
  input  CLK,
  output sum
);

  wire d_ff_2_q, FDHA_2_out, FDHA_out, HA_out_3, HA_out_4, xor_1_out, xor_2_out;

  and FDHA (FDHA_out, HA_out_3, x);
  xor xor_1 (xor_1_out, x, HA_out_3);
  D_Flip_Flop d_ff_1 (.clk(CLK), .D(xor_1_out), .Q(sum), .reset(clr));  // open: Qn, preset, en
  HA HA (.in_1(y), .in_2(d_ff_2_q), .out_3(HA_out_3), .out_4(HA_out_4));
  xor xor_2 (xor_2_out, HA_out_4, FDHA_out);
  D_Flip_Flop d_ff_2 (.clk(CLK), .D(xor_2_out), .Q(d_ff_2_q), .reset(clr));  // open: Qn, preset, en
  and FDHA_2 (FDHA_2_out, FDHA_out, HA_out_4);

  // Notes on the sheet:
  //   sc
endmodule

module counter (
  input  clk,
  output out_2
);

  wire comparator_1_eq;
  wire [3:0] counter_1_q;

  Counter #(.width(4), .max('h8), .ongoal("stay")) counter_1 (
    .Q(counter_1_q), .clk(clk));  // open: load, D, count, carry, clr
  Comparator #(.width(4)) comparator_1 (.a(counter_1_q), .b(4'b1001), .eq(comparator_1_eq));  // open: gt, lt
  and and_1 (out_2, comparator_1_eq, clk);
endmodule

module mainnn (
  input  X7,
  input  X6,
  input  X5,
  input  X4,
  input  X3,
  input  X2,
  input  X1,
  input  X0,
  input  crl,
  input  in_10
);

  wire and_1_out, and_2_out, and_3_out, and_4_out, and_5_out, and_6_out, and_7_out, and_8_out, clock_1_out,
       comparator_1_eq, comparator_2_eq, csa_1_sum, csa_2_sum, csa_3_sum, csa_4_sum, csa_5_sum, csa_6_sum,
       csa_7_sum, not_1_out, not_2_out, shift_register_1_out, shift_register_2_q0, tcmp_1_out_4,
       unit_digit_1_g;
  wire [3:0] counter_1_q;
  wire [4:0] counter_2_q;

  Clock clock_1 (.out(clock_1_out));
  Counter #(.width(4), .max('h7), .ongoal("stay")) counter_1 (
    .Q(counter_1_q), .clk(clock_1_out));  // open: load, D, count, carry, clr
  Comparator #(.width(4)) comparator_1 (.a(counter_1_q), .b(4'b1000), .eq(comparator_1_eq));  // open: gt, lt
  not not_1 (not_1_out, comparator_1_eq);
  Shift_Register shift_register_1 (
    .shift(not_1_out), .clk(clock_1_out), .out(shift_register_1_out));  // open: in, load, clr, d0, q0, d1, q1, d2, q2, d3, q3, d4, q4, d5, q5, d6, q6, d7, q7
  and and_1 (and_1_out, shift_register_1_out, X7);
  and and_2 (and_2_out, shift_register_1_out, X6);
  TCMP tcmp_1 (.A(and_1_out), .reset(crl), .out_4(tcmp_1_out_4), .clk(clock_1_out));
  and and_3 (and_3_out, shift_register_1_out, X5);
  CSA csa_1 (.x(and_2_out), .y(tcmp_1_out_4), .clr(crl), .CLK(clock_1_out), .sum(csa_1_sum));
  and and_4 (and_4_out, shift_register_1_out, X3);
  and and_5 (and_5_out, shift_register_1_out, X4);
  CSA csa_2 (.x(and_3_out), .y(csa_1_sum), .clr(crl), .CLK(clock_1_out), .sum(csa_2_sum));
  and and_6 (and_6_out, shift_register_1_out, X2);
  CSA csa_3 (.x(and_5_out), .y(csa_2_sum), .clr(crl), .CLK(clock_1_out), .sum(csa_3_sum));
  CSA csa_4 (.x(and_4_out), .y(csa_3_sum), .clr(crl), .CLK(clock_1_out), .sum(csa_4_sum));
  and and_7 (and_7_out, shift_register_1_out, X1);
  CSA csa_5 (.x(and_6_out), .y(csa_4_sum), .clr(crl), .CLK(clock_1_out), .sum(csa_5_sum));
  and and_8 (and_8_out, shift_register_1_out, X0);
  CSA csa_6 (.x(and_7_out), .y(csa_5_sum), .clr(crl), .CLK(clock_1_out), .sum(csa_6_sum));
  CSA csa_7 (.x(and_8_out), .y(csa_6_sum), .clr(crl), .CLK(clock_1_out), .sum(csa_7_sum));
  Shift_Register #(.length(16)) shift_register_2 (
    .shift(not_2_out), .in(csa_7_sum), .clk(clock_1_out), .clr(crl), .q0(shift_register_2_q0));  // open: out, load, d0, d1, q1, d2, q2, d3, q3, d4, q4, d5, q5, d6, q6, d7, q7, d8, q8, d9, q9, d10, q10, d11, q11, d12, q12, d13, q13, d14, q14, d15, q15
  Counter #(.width(5), .max('h11), .ongoal("stay")) counter_2 (
    .Q(counter_2_q), .clk(clock_1_out));  // open: load, D, count, carry, clr
  unit_digit unit_digit_1 (
    .p3(shift_register_2_q0), .p2(in_10), .p1(in_10), .p0(in_10), .g(unit_digit_1_g));  // open: a, b, c, d, e, f
  not not_2 (not_2_out, comparator_2_eq);
  Comparator #(.width(5), .mode("unsigned")) comparator_2 (
    .a(counter_2_q), .b(5'b10001), .eq(comparator_2_eq));  // open: gt, lt
  _7_Segment_Display u_7_segment_display_1 (.g(unit_digit_1_g));  // open: f, a, b, e, d, c, dp
endmodule
